// Logisim project M4_8.1.circ as structural Verilog: 2 circuits, main circuit main
module main (
);

  wire ABUSHL, ABUSPC, ABUSSP, and_2_out, CLK, clock_1_out, comparator_1_eq, d_ff_2_qn, DBUSA, DBUSB, DBUSH,
       DBUSL, DBUSPCH, DBUSPCL, DBUSSPH, DBUSSPL, DBUST, demultiplexer_3_out1, DREAD, DWRITE, HALT, LOADA,
       LOADB, LOADH, LOADL, LOADPC, LOADSP, LOADT, nor_1_out, nor_2_out, nor_3_out, not_1_out, nPOR, NXTI,
       or_1_out, or_2_out, or_4_out, PCINC, PH0, PH1, PH2, PH3, POR, por_1_out, RAMREAD, RAMWRITE, RUN,
       RUNNING, SS, STOP;
  wire [1:0] PH;
  wire [1:1] and_1_out;
  wire [3:0] bit_extender_1_out;
  wire [7:0] A_q, B_q, BOOTROM_data, DATA, H_q, IR, L_q, ram_1_p4;
  wire [15:0] AD, PC;
  wire [15:3] IDECODE_data;
  wire [15:8] DATA16;

  Clock clock_1 (.out(clock_1_out));
  or or_1 (or_1_out, POR, STOP, HALT);
  POR #(.PorHighDuration(1)) por_1 (.out(por_1_out));
  and and_1 (and_1_out[1], clock_1_out, nPOR);
  nor nor_1 (nor_1_out, RUN, nor_2_out);
  nor nor_2 (nor_2_out, nor_1_out, or_1_out);
  D_Flip_Flop d_ff_1 (.D(nor_2_out), .clk(clock_1_out), .Q(RUNNING));  // open: Qn, preset, reset
  or or_2 (or_2_out, PH0, PCINC);
  nor nor_3 (nor_3_out, AD[15], AD[14], AD[13], AD[12], AD[11], AD[10]);
  ROM #(.addrWidth(10)) BOOTROM (.addr(AD[9:0]), .data(BOOTROM_data));
  D_Flip_Flop #(.trigger("falling")) d_ff_2 (
    .D(not_1_out), .clk(clock_1_out), .Qn(d_ff_2_qn));  // open: Q, preset, reset
  not not_1 (not_1_out, por_1_out);
  BitSelector #(.width(2)) bitselector_1 (.in({and_1_out[1], SS}), .out(CLK), .sel(RUNNING));
  Counter #(.max('hffff), .width(16)) u_PC (
    .clr(POR), .load(LOADPC), .count(or_2_out), .clk(CLK), .D({DATA16, DATA}), .Q(PC));  // open: up, carry
  Counter #(.max('h3), .width(2)) PHASECOUNTER (
    .clr(POR), .load(NXTI), .clk(CLK), .D(2'b00), .Q(PH));  // open: up, count, carry
  or or_3 (POR, por_1_out, d_ff_2_qn);
  not not_2 (nPOR, POR);
  assign AD = or_4_out ? PC : 16'bz;  // Controlled_Buffer controlled_buffer_1
  or or_4 (or_4_out, PH0, ABUSPC);
  and and_2 (and_2_out, nor_3_out, DREAD);
  assign DATA = and_2_out ? BOOTROM_data : 8'bz;  // Controlled_Buffer controlled_buffer_2
  Decoder #(.select(2)) decoder_1 (.out0(PH0), .out1(PH1), .out2(PH2), .out3(PH3), .sel(PH), .en(nPOR));
  Register u_IR (.D(DATA), .en(PH0), .clk(CLK), .Q(IR), .clr(POR));
  // RAM #(.addrWidth(10), .databus("bidir"), .enables("line"), .\type ("nonvolatile")) ram_1: pin names not known; wires that end beside it: AD[9:0], RAMREAD, RAMWRITE, ram_1_p4
  LED led_1 (.in(RUNNING));
  Register T (.D(DATA), .en(LOADT), .clk(CLK), .Q(DATA16));  // open: clr
  Comparator #(.width(6)) comparator_1 (.a({6{1'b1}}), .b(AD[15:10]), .eq(comparator_1_eq));  // open: gt, lt
  LED led_2 (.in(POR));
  Button button_1 (.out(RUN));
  ROM #(.addrWidth(10), .dataWidth(16)) IDECODE (.addr({IR, PH}), .data({IDECODE_data, HALT, PCINC, NXTI}));
  LED led_3 (.in(CLK));
  Hex_Digit_Display hex_digit_display_1 (.value(PC[15:12]));  // open: dp
  and and_3 (RAMREAD, DREAD, comparator_1_eq);
  and and_4 (RAMWRITE, comparator_1_eq, DWRITE);
  Hex_Digit_Display hex_digit_display_2 (.value(PC[11:8]));  // open: dp
  Hex_Digit_Display hex_digit_display_3 (.value(PC[7:4]));  // open: dp
  Button button_2 (.out(STOP));
  assign DATA = RAMREAD ? ram_1_p4 : 8'bz;  // Controlled_Buffer controlled_buffer_3
  assign ram_1_p4 = RAMWRITE ? DATA : 8'bz;  // Controlled_Buffer controlled_buffer_4
  Hex_Digit_Display hex_digit_display_4 ();  // open: value, dp
  Hex_Digit_Display hex_digit_display_5 (.value(PC[3:0]));  // open: dp
  Button button_3 (.out(SS));
  Hex_Digit_Display hex_digit_display_6 (.value(IR[7:4]));  // open: dp
  Hex_Digit_Display hex_digit_display_7 (.value(IR[3:0]));  // open: dp
  Hex_Digit_Display hex_digit_display_8 (.value(bit_extender_1_out));  // open: dp
  assign bit_extender_1_out = {{2{1'b0}}, PH};  // Bit_Extender bit_extender_1
  Hex_Digit_Display hex_digit_display_9 (.value(DATA[7:4]));  // open: dp
  Hex_Digit_Display hex_digit_display_10 (.value(DATA[3:0]));  // open: dp
  Register A (.D(DATA), .en(LOADA), .clk(CLK), .Q(A_q));  // open: clr
  Register B (.D(DATA), .en(LOADB), .clk(CLK), .Q(B_q));  // open: clr
  Register H (.D(DATA), .en(LOADH), .clk(CLK), .Q(H_q));  // open: clr
  Register L (.D(DATA), .en(LOADL), .clk(CLK), .Q(L_q));  // open: clr
  Demultiplexer #(.select(2)) demultiplexer_1 (
    .out1(ABUSPC), .out2(ABUSSP), .out3(ABUSHL), .in(1'b1), .sel(IDECODE_data[7:6]));  // open: out0
  Demultiplexer #(.select(4)) demultiplexer_2 (
    .out1(DWRITE), .out2(LOADPC), .out3(LOADSP), .out4(LOADT), .out5(LOADA), .out6(LOADB), .out7(LOADH),
    .out8(LOADL), .in(1'b1), .sel(IDECODE_data[11:8]));  // open: out0, out9, out10, out11, out12, out13, out14, out15
  Demultiplexer #(.select(4)) demultiplexer_3 (
    .out1(demultiplexer_3_out1), .out2(DBUSPCH), .out3(DBUSPCL), .out4(DBUSSPH), .out5(DBUSSPL),
    .out6(DBUST), .out7(DBUSA), .out8(DBUSB), .out9(DBUSH), .out10(DBUSL), .in(1'b1),
    .sel(IDECODE_data[15:12]));  // open: out0, out11, out12, out13, out14, out15
  assign DATA = DBUSA ? A_q : 8'bz;  // Controlled_Buffer controlled_buffer_5
  assign DATA = DBUSB ? B_q : 8'bz;  // Controlled_Buffer controlled_buffer_6
  assign DATA = DBUSH ? H_q : 8'bz;  // Controlled_Buffer controlled_buffer_7
  assign DATA = DBUSL ? L_q : 8'bz;  // Controlled_Buffer controlled_buffer_8
  or or_5 (DREAD, PH0, demultiplexer_3_out1);

  // Other names for the same wires on the sheet: DATA16[7:0] = DATA

  // Notes on the sheet:
  //   contents of BOOTROM (hex, n*v repeats v):
  //   1 80 10 0 0 0 1 0 80
  //   RUN
  //   RST
  //   contents of IDECODE (hex, n*v repeats v):
  //   0 1 0 0 0 1543 59*0 7601 447*0 442 241 506*0 5
  //   CLK
  //   PC
  //   IR
  //   PH
endmodule

module Pulsator (
  input  P_IN,
  input  CLK,
  input  RST,
  output P_OUT
);

  wire d_ff_1_qn;

  D_Flip_Flop d_ff_1 (.D(P_IN), .clk(CLK), .Qn(d_ff_1_qn), .reset(RST));  // open: Q, preset
  and and_1 (P_OUT, P_IN, d_ff_1_qn);
endmodule
